# Fritzing sketch energy (saved by Fritzing 0.9.3b)
breadboards: 1

parts:
  U1 = NodeMCU V1.0
  Part1 = ACS712 Current Sensor Module
  Part3 = Lilypad Battery Connect
  LED1 = LEDs [package=led10mm]

nets:
  3V3: U1.3V3, Part1.VCC
  GND: U1.GND, Part1.GND
  N1: U1.A0, Part1.OUT
  N2: Part1.INPUT+, LED1.A
  N3: Part1.INPUT-, Part3.+
  N4: Part3.-, LED1.C

notes:
  240V AC power supply

custom parts:
  NodeMCU V1.0: ESP8266 based NodeMCU
  LEDs: LEDs Standard schematic elements and footprints for 5mm, 3mm, 1206, and 0603 sized LEDs. 5mm - Spark Fun Electronics SKU : COM-00529 (and others)
